# Fritzing sketch 12v realy (saved by Fritzing 0.9.3b)

parts:
  U1 = ESP32S-HiLetgo [part_number=ESP32S-HiLetgo]
  V1 = DC Power  # not connected
  JACK1 = 2.1mm Barrel Jack with Terminal Block
  8_Channel_Relay1 = 8 Channel Power Relay

nets:
  N1: U1.3.3, 8_Channel_Relay1.VCC#17
  N2: U1.GPIO32, 8_Channel_Relay1.IN8
  N3: U1.GPIO33, 8_Channel_Relay1.IN7
  N4: U1.GPIO25, 8_Channel_Relay1.IN6
  N5: U1.GPIO26, 8_Channel_Relay1.IN5
  N6: U1.GPIO27, 8_Channel_Relay1.IN4
  N7: U1.GPIO14, 8_Channel_Relay1.IN3
  N8: U1.GPIO12, 8_Channel_Relay1.IN2
  N9: U1.GPIO13, 8_Channel_Relay1.IN1
  N10: U1.VIN, 8_Channel_Relay1.VCC#19
  N11: U1.GND, 8_Channel_Relay1.GND#8
  N12: JACK1.POS, 8_Channel_Relay1.JD-VCC
  N13: JACK1.NEG, 8_Channel_Relay1.GND#18

custom parts:
  ESP32S-HiLetgo: HiLetgo ESP-WROOM-32 ESP32 ESP-32S Development Board 2.4GHz Dual-Mode WiFi + Bluetooth Dual Cores Microcontroller The ESP32 integrated with Antenna switches, RF Balun, power amplifiers, low-noise amplifiers, filters, and management modules, and the entire solution occupies the least area of PCB. 2.4 GHz Wi-Fi plus Bluetooth dual-mode chip, with TSMC Ultra-low power consumption 40nm technology,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
  DC Power: A generic dc power symbol
  8 Channel Power Relay: An 8 channel power relay. The module operates at 5V.
